// Logisim project atodCircuit.circ as structural Verilog: 1 circuit, main circuit main
module main (
  input  Dout,
  input  [7:0] register,
  output clock,
  output cs,
  output Din
);

  wire and_1_out, and_2_out, and_4_out, and_5_out, count_out, decoder_1_out5, decoder_1_out6, decoder_1_out7,
       decoder_out, msbf, na, not_1_out, not_2_out, not_3_out, or_1_out, ready_for_out, shift_register_1_out,
       single, start_bit, which_controller;
  wire [7:0] counter_1_q, counter_2_q;

  Clock clock_1 (.out(clock));
  Counter counter_1 (
    .Q({counter_1_q[7:5], cs, count_out, counter_1_q[2:0]}), .clk(clock), .clr(counter_1_q[5]));  // open: load, D, count, carry, preset, down
  and and_1 (and_1_out, register[0], which_controller);
  or or_1 (or_1_out, decoder_out, count_out);
  Counter counter_2 (.Q(counter_2_q), .clk(and_2_out), .clr(not_1_out));  // open: load, D, count, carry, preset, down
  and and_2 (and_2_out, clock, ready_for_out);
  not not_1 (not_1_out, ready_for_out);
  Decoder #(.select(3), .enable("false")) decoder_1 (
    .out0(na), .out1(start_bit), .out2(single), .out3(which_controller), .out4(msbf), .out5(decoder_1_out5),
    .out6(decoder_1_out6), .out7(decoder_1_out7), .sel(counter_1_q[2:0]));
  or or_2 (Din, start_bit, single, and_1_out, msbf);
  and and_3 (ready_for_out, or_1_out, not_2_out);
  not not_2 (not_2_out, cs);
  and and_4 (and_4_out, counter_2_q[3], counter_2_q[2]);
  or or_3 (decoder_out, decoder_1_out5, decoder_1_out6, decoder_1_out7);
  not not_3 (not_3_out, and_4_out);
  Shift_Register shift_register_1 (
    .in(Dout), .clk(and_5_out), .out(shift_register_1_out));  // open: shift, load, clr, d0, q0, d1, q1, d2, q2, d3, q3, d4, q4, d5, q5, d6, q6, d7, q7
  and and_5 (and_5_out, and_2_out, not_3_out);
  Shift_Register shift_register_2 (
    .in(shift_register_1_out), .clk(and_5_out));  // open: shift, out, load, clr, d0, q0, d1, q1, d2, q2, d3, q3, d4, q4, d5, q5, d6, q6, d7, q7

  // Other names for the same wires on the sheet: select_bit = register[0]

  // Notes on the sheet:
  //   7 or gates
  //   5 and gates
  //   1 decoder
  //   2 shift registers
  //   2 counters
  //   1 decoder
endmodule
