// Logisim project extraRegisterTestDesign.circ as structural Verilog: 3 circuits, main circuit main
module main (
  input  equal_high,
  input  equal_low,
  input  [3:0] bottom_4_bits,
  input  r_w_star,
  input  clock
);

  wire and_1_out, n74hct139_1_y0_star, n74hct139_1_y1_star, n74hct139_1_y2_star, n74hct139_1_y3_star,
       n74hct139_2_y0_star, n74hct139_2_y1_star, n74hct139_2_y2_star, n74hct139_2_y3_star,
       n74hct139_3_y0_star, n74hct139_3_y1_star, n74hct139_3_y2_star, n74hct139_3_y3_star,
       n74hct139_4_y0_star, n74hct139_4_y1_star, n74hct139_4_y2_star, n74hct139_4_y3_star,
       n74hct139_5_y0_star, n74hct139_5_y1_star, n74hct139_5_y2_star, n74hct139_5_y3_star, nand_1_out,
       nand_2_out, not_1_out, not_2_out, not_3_out, not_4_out, not_5_out, not_6_out, not_7_out, not_8_out,
       not_9_out, not_10_out, not_11_out, not_12_out, not_13_out, not_14_out, not_15_out, not_16_out,
       not_17_out, not_18_out, not_19_out, not_20_out, not_21_out, not_22_out, not_23_out, or_1_out;

  not not_1 (not_1_out, equal_high);
  not not_2 (not_2_out, equal_low);
  not not_3 (not_3_out, r_w_star);
  and and_1 (and_1_out, not_3_out, clock);
  nand nand_1 (nand_1_out, r_w_star, r_w_star);
  or or_1 (or_1_out, not_1_out, not_2_out);
  nand nand_2 (nand_2_out, nand_1_out, clock);
  _74hct139 u_74hct139_1 (
    .g_star(or_1_out), .a(bottom_4_bits[2]), .b(bottom_4_bits[3]), .y0_star(n74hct139_1_y0_star),
    .y1_star(n74hct139_1_y1_star), .y2_star(n74hct139_1_y2_star), .y3_star(n74hct139_1_y3_star));
  not not_4 (not_4_out, n74hct139_2_y0_star);
  _74hct139 u_74hct139_2 (
    .g_star(n74hct139_1_y0_star), .a(bottom_4_bits[0]), .b(bottom_4_bits[1]), .y0_star(n74hct139_2_y0_star),
    .y1_star(n74hct139_2_y1_star), .y2_star(n74hct139_2_y2_star), .y3_star(n74hct139_2_y3_star));
  not not_5 (not_5_out, n74hct139_2_y1_star);
  not not_6 (not_6_out, n74hct139_2_y2_star);
  not not_7 (not_7_out, n74hct139_2_y3_star);
  _74hct139 u_74hct139_3 (
    .g_star(n74hct139_1_y1_star), .a(bottom_4_bits[0]), .b(bottom_4_bits[1]), .y0_star(n74hct139_3_y0_star),
    .y1_star(n74hct139_3_y1_star), .y2_star(n74hct139_3_y2_star), .y3_star(n74hct139_3_y3_star));
  not not_8 (not_8_out, n74hct139_3_y0_star);
  not not_9 (not_9_out, n74hct139_3_y1_star);
  not not_10 (not_10_out, n74hct139_3_y2_star);
  not not_11 (not_11_out, n74hct139_3_y3_star);
  _74hct139 u_74hct139_4 (
    .g_star(n74hct139_1_y2_star), .a(bottom_4_bits[0]), .b(bottom_4_bits[1]), .y0_star(n74hct139_4_y0_star),
    .y1_star(n74hct139_4_y1_star), .y2_star(n74hct139_4_y2_star), .y3_star(n74hct139_4_y3_star));
  not not_12 (not_12_out, n74hct139_4_y0_star);
  not not_13 (not_13_out, n74hct139_4_y1_star);
  not not_14 (not_14_out, n74hct139_4_y2_star);
  not not_15 (not_15_out, n74hct139_4_y3_star);
  _74hct139 u_74hct139_5 (
    .g_star(n74hct139_1_y3_star), .a(bottom_4_bits[0]), .b(bottom_4_bits[1]), .y0_star(n74hct139_5_y0_star),
    .y1_star(n74hct139_5_y1_star), .y2_star(n74hct139_5_y2_star), .y3_star(n74hct139_5_y3_star));
  not not_16 (not_16_out, n74hct139_5_y0_star);
  not not_17 (not_17_out, n74hct139_5_y1_star);
  not not_18 (not_18_out, n74hct139_5_y2_star);
  not not_19 (not_19_out, n74hct139_5_y3_star);
  // AND_Gate and_2 has open pins: in0=not_4_out, in1=and_1_out, out=open
  // AND_Gate and_3 has open pins: in0=not_5_out, in1=and_1_out, out=open
  // AND_Gate and_4 has open pins: in0=not_6_out, in1=and_1_out, out=open
  // AND_Gate and_5 has open pins: in0=not_7_out, in1=and_1_out, out=open
  // AND_Gate and_6 has open pins: in0=not_8_out, in1=and_1_out, out=open
  // AND_Gate and_7 has open pins: in0=not_9_out, in1=and_1_out, out=open
  // AND_Gate and_8 has open pins: in0=not_10_out, in1=and_1_out, out=open
  // AND_Gate and_9 has open pins: in0=not_11_out, in1=and_1_out, out=open
  // AND_Gate and_10 has open pins: in0=not_12_out, in1=and_1_out, out=open
  // AND_Gate and_11 has open pins: in0=not_13_out, in1=and_1_out, out=open
  // AND_Gate and_12 has open pins: in0=not_14_out, in1=and_1_out, out=open
  // AND_Gate and_13 has open pins: in0=not_15_out, in1=and_1_out, out=open
  // AND_Gate and_14 has open pins: in0=not_16_out, in1=and_1_out, out=open
  // AND_Gate and_15 has open pins: in0=not_17_out, in1=and_1_out, out=open
  // AND_Gate and_16 has open pins: in0=not_18_out, in1=and_1_out, out=open
  // AND_Gate and_17 has open pins: in0=not_19_out, in1=and_1_out, out=open
  not not_20 (not_20_out, not_4_out);
  not not_21 (not_21_out, not_5_out);
  not not_22 (not_22_out, not_6_out);
  not not_23 (not_23_out, not_7_out);
  // NOR_Gate nor_1 has open pins: in0=not_20_out, in1=nand_2_out, out=open
  // NOR_Gate nor_2 has open pins: in0=not_21_out, in1=nand_2_out, out=open
  // NOR_Gate nor_3 has open pins: in0=not_22_out, in1=nand_2_out, out=open
  // NOR_Gate nor_4 has open pins: in0=not_23_out, in1=nand_2_out, out=open
endmodule

module _74hct139 (
  input  g_star,
  input  a,
  input  b,
  output y0_star,
  output y1_star,
  output y2_star,
  output y3_star
);

  wire decoder_1_out0, decoder_1_out1, decoder_1_out2, decoder_1_out3, not_1_out;

  not not_1 (not_1_out, g_star);
  Decoder #(.select(2)) decoder_1 (
    .out0(decoder_1_out0), .out1(decoder_1_out1), .out2(decoder_1_out2), .out3(decoder_1_out3), .sel({b, a}),
    .en(not_1_out));
  Pull_Resistor pull_resistor_1 (.node(decoder_1_out0));
  not not_2 (y0_star, decoder_1_out0);
  not not_3 (y1_star, decoder_1_out1);
  Pull_Resistor pull_resistor_2 (.node(decoder_1_out1));
  not not_4 (y2_star, decoder_1_out2);
  Pull_Resistor pull_resistor_3 (.node(decoder_1_out2));
  Pull_Resistor pull_resistor_4 (.node(decoder_1_out3));
  not not_5 (y3_star, decoder_1_out3);
endmodule

module working_circuit (
  input  equal_high,
  input  equal_low,
  input  [3:0] bottom_4_bits,
  input  r_w_star,
  input  clock
);

  wire and_1_out, n74hct139_1_y0_star, n74hct139_1_y1_star, n74hct139_1_y2_star, n74hct139_1_y3_star,
       n74hct139_2_y0_star, n74hct139_2_y1_star, n74hct139_2_y2_star, n74hct139_2_y3_star,
       n74hct139_3_y0_star, n74hct139_3_y1_star, n74hct139_3_y2_star, n74hct139_3_y3_star,
       n74hct139_4_y0_star, n74hct139_4_y1_star, n74hct139_4_y2_star, n74hct139_4_y3_star,
       n74hct139_5_y0_star, n74hct139_5_y1_star, n74hct139_5_y2_star, n74hct139_5_y3_star, not_1_out,
       not_2_out, not_3_out, not_4_out, not_5_out, not_6_out, not_7_out, not_8_out, not_9_out, not_10_out,
       not_11_out, not_12_out, not_13_out, not_14_out, not_15_out, not_16_out, not_17_out, not_18_out,
       not_19_out, or_1_out;

  not not_1 (not_1_out, equal_high);
  not not_2 (not_2_out, equal_low);
  not not_3 (not_3_out, r_w_star);
  and and_1 (and_1_out, not_3_out, clock);
  or or_1 (or_1_out, not_2_out, not_1_out);
  _74hct139 u_74hct139_1 (
    .g_star(or_1_out), .a(bottom_4_bits[2]), .b(bottom_4_bits[3]), .y0_star(n74hct139_1_y0_star),
    .y1_star(n74hct139_1_y1_star), .y2_star(n74hct139_1_y2_star), .y3_star(n74hct139_1_y3_star));
  not not_4 (not_4_out, n74hct139_2_y0_star);
  _74hct139 u_74hct139_2 (
    .g_star(n74hct139_1_y0_star), .a(bottom_4_bits[0]), .b(bottom_4_bits[1]), .y0_star(n74hct139_2_y0_star),
    .y1_star(n74hct139_2_y1_star), .y2_star(n74hct139_2_y2_star), .y3_star(n74hct139_2_y3_star));
  not not_5 (not_5_out, n74hct139_2_y1_star);
  not not_6 (not_6_out, n74hct139_2_y2_star);
  not not_7 (not_7_out, n74hct139_2_y3_star);
  not not_8 (not_8_out, n74hct139_3_y0_star);
  _74hct139 u_74hct139_3 (
    .g_star(n74hct139_1_y1_star), .a(bottom_4_bits[0]), .b(bottom_4_bits[1]), .y0_star(n74hct139_3_y0_star),
    .y1_star(n74hct139_3_y1_star), .y2_star(n74hct139_3_y2_star), .y3_star(n74hct139_3_y3_star));
  not not_9 (not_9_out, n74hct139_3_y1_star);
  not not_10 (not_10_out, n74hct139_3_y2_star);
  not not_11 (not_11_out, n74hct139_3_y3_star);
  _74hct139 u_74hct139_4 (
    .g_star(n74hct139_1_y2_star), .a(bottom_4_bits[0]), .b(bottom_4_bits[1]), .y0_star(n74hct139_4_y0_star),
    .y1_star(n74hct139_4_y1_star), .y2_star(n74hct139_4_y2_star), .y3_star(n74hct139_4_y3_star));
  not not_12 (not_12_out, n74hct139_4_y0_star);
  not not_13 (not_13_out, n74hct139_4_y1_star);
  not not_14 (not_14_out, n74hct139_4_y2_star);
  not not_15 (not_15_out, n74hct139_4_y3_star);
  _74hct139 u_74hct139_5 (
    .g_star(n74hct139_1_y3_star), .a(bottom_4_bits[0]), .b(bottom_4_bits[1]), .y0_star(n74hct139_5_y0_star),
    .y1_star(n74hct139_5_y1_star), .y2_star(n74hct139_5_y2_star), .y3_star(n74hct139_5_y3_star));
  not not_16 (not_16_out, n74hct139_5_y0_star);
  not not_17 (not_17_out, n74hct139_5_y1_star);
  not not_18 (not_18_out, n74hct139_5_y2_star);
  not not_19 (not_19_out, n74hct139_5_y3_star);
  // AND_Gate and_2 has open pins: in0=not_4_out, in1=and_1_out, out=open
  // AND_Gate and_3 has open pins: in0=not_5_out, in1=and_1_out, out=open
  // AND_Gate and_4 has open pins: in0=not_6_out, in1=and_1_out, out=open
  // AND_Gate and_5 has open pins: in0=not_7_out, in1=and_1_out, out=open
  // AND_Gate and_6 has open pins: in0=not_8_out, in1=and_1_out, out=open
  // AND_Gate and_7 has open pins: in0=not_9_out, in1=and_1_out, out=open
  // AND_Gate and_8 has open pins: in0=not_10_out, in1=and_1_out, out=open
  // AND_Gate and_9 has open pins: in0=not_11_out, in1=and_1_out, out=open
  // AND_Gate and_10 has open pins: in0=not_12_out, in1=and_1_out, out=open
  // AND_Gate and_11 has open pins: in0=not_13_out, in1=and_1_out, out=open
  // AND_Gate and_12 has open pins: in0=not_14_out, in1=and_1_out, out=open
  // AND_Gate and_13 has open pins: in0=not_15_out, in1=and_1_out, out=open
  // AND_Gate and_14 has open pins: in0=not_16_out, in1=and_1_out, out=open
  // AND_Gate and_15 has open pins: in0=not_17_out, in1=and_1_out, out=open
  // AND_Gate and_16 has open pins: in0=not_18_out, in1=and_1_out, out=open
  // AND_Gate and_17 has open pins: in0=not_19_out, in1=and_1_out, out=open
endmodule
