// Logisim project video.circ as structural Verilog: 1 circuit, main circuit main
module main (
  input  in_clock,
  input  [7:0] data_in,
  input  instruction,
  input  enable,
  output [7:0] out_5
);

  wire and_1_out, and_2_out, and_3_out, and_4_out, and_5_out, not_1_out, or_1_out;
  wire [1:0] state_q;
  wire [5:0] counter_2_q;
  wire [7:0] adder_1_out, counter_1_q, rom_1_data, x_2_q, x_q;

  not not_1 (not_1_out, instruction);
  and and_1 (and_1_out, in_clock, not_1_out);
  and and_2 (and_2_out, in_clock, instruction);
  or or_1 (or_1_out, and_5_out, and_4_out);
  and and_3 (and_3_out, and_1_out, rom_1_data[2]);
  Register #(.width(2), .Select("low")) state (.D(data_in[7:6]), .Q(state_q), .clk(and_2_out));  // open: en, clr
  Register #(.Select("low")) x (.D(data_in), .Q(x_q), .clk(and_4_out));  // open: en, clr
  and and_4 (and_4_out, in_clock, rom_1_data[0]);
  Register #(.Select("low")) x_2 (.D(data_in), .Q(x_2_q), .clk(and_5_out));  // open: en, clr
  and and_5 (and_5_out, in_clock, rom_1_data[1]);
  Counter counter_1 (.Q(counter_1_q), .clk(and_3_out), .clr(or_1_out));  // open: load, D, count, carry, preset, down
  Counter #(.width(6), .max('h3f)) counter_2 (
    .Q(counter_2_q), .clk(in_clock), .clr(and_2_out));  // open: load, D, count, carry, preset, down
  Register #(.width(2), .Select("low")) mode (.D(data_in[7:6]));  // open: en, Q, clk, clr
  Adder adder_1 (.a({x_2_q[3:0], x_q[3:0]}), .b(counter_1_q), .out(adder_1_out));  // open: cin, cout
  ROM #(.Select("low")) rom_1 (.addr({counter_2_q, state_q}), .data(rom_1_data));
  RAM #(.bus("separate"), .simpleMode("false"), .Select("low")) ram_1 (
    .addr(adder_1_out), .din(data_in), .str(rom_1_data[2]), .clk(and_1_out));  // open: data, sel, ld, clr
  Controlled_Buffer #(.width(8)) controlled_buffer_1 (.out(out_5), .en(enable));  // open: in
endmodule
